# Fritzing sketch morse (saved by Fritzing 0.9.3b)
breadboards: 1

parts:
  Composant1 = Arduino Due (Rev2b)
  R1 = Resistor [tolerance=±5% resistance=220 package=THT]  # not connected
  LED1 = LED - 5mm [color="Yellow (595nm)" package="5 mm [THT]"]
  LED2 = LED - 5mm [color="Red (633nm)" package="5 mm [THT]"]
  R2 = Resistor [tolerance=±5% resistance=220 package=THT]
  R3 = Resistor [tolerance=±5% resistance=220 package=THT]  # not connected
  S2 = Pushbutton [package="[THT]"]
  LED10 = LED - 5mm [color="Yellow (595nm)" package="5 mm [THT]"]
  LED11 = LED - 5mm [color="Yellow (595nm)" package="5 mm [THT]"]
  S8 = Pushbutton [package="[THT]"]
  R23 = Resistor [tolerance=±5% resistance=220 package=THT]
  R24 = Resistor [tolerance=±5% resistance=220 package=THT]
  R25 = Resistor [tolerance=±5% resistance=220 package=THT]
  R26 = Resistor [tolerance=±5% resistance=220 package=THT]

nets:
  N1: Composant1.D44, LED11.anode
  N2: Composant1.D45, S8.Pin_3, S8.Pin_4, R26.Pin_1
  N3: Composant1.D46, LED10.anode
  N4: Composant1.D47, S2.Pin_3, S2.Pin_4, R25.Pin_1
  N5: Composant1.D49, LED2.anode
  N6: Composant1.D51, LED1.anode
  N7: Composant1.GND, R2.Pin_0, R23.Pin_0, R24.Pin_0, R25.Pin_0, R26.Pin_0
  N8: LED2.cathode, R2.Pin_1
  N9: S2.Pin_1, S2.Pin_2, S8.Pin_1, S8.Pin_2
  N10: LED10.cathode, R23.Pin_1
  N11: LED11.cathode, R24.Pin_1
