# Fritzing sketch piano (saved by Fritzing 0.9.3b)
breadboards: 1

parts:
  Composant1 = Arduino Due (Rev2b)
  LED4 = LED - 5mm [color="Yellow (595nm)" package="5 mm [THT]"]  # not connected
  LED5 = LED - 5mm [color="Green (570nm)" package="5 mm [THT]"]
  LED6 = LED - 5mm [color="Red (635nm)" package="5 mm [THT]"]
  R11 = Resistor [tolerance=±5% resistance=220 package=THT]
  R12 = Resistor [tolerance=±5% resistance=220 package=THT]
  R13 = Resistor [tolerance=±5% resistance=220 package=THT]
  S3 = Pushbutton [package="[THT]"]
  S4 = Pushbutton [package="[THT]"]
  S5 = Pushbutton [package="[THT]"]
  S6 = Pushbutton [package="[THT]"]
  S7 = Pushbutton [package="[THT]"]
  R14 = Resistor [tolerance=±2% resistance=1k package=THT]
  R16 = Resistor [tolerance=±5% resistance=560 package=THT]
  R17 = Resistor [tolerance=±5% resistance=4.7k package=THT]
  R18 = Resistor [tolerance=±5% resistance=10k package=THT]
  J1 = Piezo Speaker
  R19 = Resistor [tolerance=±5% resistance=1k package=THT]
  R15 = Resistor [tolerance=±5% resistance=15k power=1kW package=THT]
  LED7 = LED - 5mm [color="Red (633nm)" package="5 mm [THT]"]
  LED8 = LED - 5mm [color="Green (570nm)" package="5 mm [THT]"]
  R20 = Resistor [tolerance=±5% resistance=220 package=THT]
  R21 = Resistor [tolerance=±5% resistance=220 package=THT]
  LED9 = LED - 5mm [color="Blue (525nm)" package="5 mm [THT]"]  # not connected
  R22 = Resistor [tolerance=±5% resistance=220 package=THT]

nets:
  N1: Composant1.A1, S3.Pin_1, S3.Pin_2, S4.Pin_1, S4.Pin_2, S5.Pin_1, S5.Pin_2, S6.Pin_1, S6.Pin_2, S7.Pin_1, S7.Pin_2, R14.Pin_0
  N2: Composant1.D14/TX3, LED5.anode
  N3: Composant1.D17/RX2, LED7.anode
  N4: Composant1.D18/TX1, LED8.anode
  N5: Composant1.D19/RX1, LED6.anode
  N6: Composant1.IOREF, R14.Pin_1, J1.pin2
  N7: Composant1.SCL1, R11.Pin_1, R12.Pin_1, R13.Pin_1, R16.Pin_1, R17.Pin_1, R18.Pin_1, J1.pin1, R19.Pin_1, R15.Pin_1, R20.Pin_0, R21.Pin_0, R22.Pin_1
  N8: LED5.cathode, R13.Pin_0
  N9: LED6.cathode, R12.Pin_0
  N10: S3.Pin_3, S3.Pin_4, R17.Pin_0
  N11: S4.Pin_3, S4.Pin_4, R19.Pin_0
  N12: S5.Pin_3, S5.Pin_4, R16.Pin_0
  N13: S6.Pin_3, S6.Pin_4, R18.Pin_0
  N14: S7.Pin_3, S7.Pin_4, R15.Pin_0
  N15: LED7.cathode, R20.Pin_1
  N16: LED8.cathode, R21.Pin_1
