# Fritzing sketch schema_a_finir - Copie (saved by Fritzing 0.9.3b)
breadboards: 2

parts:
  Composant1 = Arduino Due (Rev2b)
  R1 = Resistor [tolerance=±5% resistance=220 package=THT]
  LED1 = LED - 5mm [color="Red (633nm)" package="5 mm [THT]"]
  LED2 = LED - 5mm [color="Green (570nm)" package="5 mm [THT]"]
  R2 = Resistor [tolerance=±5% resistance=220 package=THT]
  S1 = Pushbutton [package="[THT]"]
  R3 = Resistor [tolerance=±5% resistance=220 package=THT]
  LED3 = 7-SEGMENT-4DIGIT-YOUNGSUN [package=7-segment-4digit-youngsun]
  R4 = Resistor [tolerance=±5% resistance=220 package=THT]
  R5 = Resistor [tolerance=±5% resistance=220 package=THT]
  R8 = Resistor [tolerance=±5% resistance=220 package=THT]
  R9 = Resistor [tolerance=±5% resistance=220 package=THT]
  R10 = Resistor [tolerance=±5% resistance=220 package=THT]
  S2 = Pushbutton [package="[THT]"]
  LED4 = LED - 5mm [color="Red (633nm)" package="5 mm [THT]"]
  LED5 = LED - 5mm [color="Green (570nm)" package="5 mm [THT]"]
  LED6 = LED - 5mm [color="Blue (525nm)" package="5 mm [THT]"]
  R11 = Resistor [tolerance=±5% resistance=220 package=THT]
  R12 = Resistor [tolerance=±5% resistance=220 package=THT]
  R13 = Resistor [tolerance=±5% resistance=220 package=THT]
  S3 = Pushbutton [package="[THT]"]
  S4 = Pushbutton [package="[THT]"]
  S5 = Pushbutton [package="[THT]"]
  S6 = Pushbutton [package="[THT]"]
  S7 = Pushbutton [package="[THT]"]
  R14 = Resistor [tolerance=±2% resistance=1k package=THT]
  R15 = Resistor [tolerance=±5% resistance=220 power=1kW package=THT]
  R16 = Resistor [tolerance=±5% resistance=560 package=THT]
  R17 = Resistor [tolerance=±5% resistance=4.7k package=THT]
  R18 = Resistor [tolerance=±5% resistance=10k package=THT]
  J1 = Piezo Speaker
  R19 = Resistor [tolerance=±5% resistance=1k package=THT]

nets:
  N1: Composant1.A0, S3.Pin_3, S3.Pin_4, S4.Pin_3, S4.Pin_4, S5.Pin_3, S5.Pin_4, S6.Pin_3, S6.Pin_4, S7.Pin_3, S7.Pin_4, R14.Pin_1
  N2: Composant1.D21/SCL3, S2.Pin_3, S2.Pin_4
  N3: Composant1.IOREF, S1.Pin_1, S1.Pin_2, R14.Pin_0
  N4: Composant1.D8_PWM, LED3.COL-A
  N5: Composant1.D9_PWM, LED3.DIG2, R5.Pin_0
  N6: Composant1.D10_PWM/SS0, LED3.DIG1
  N7: Composant1.D11_PWM, LED3.A
  N8: Composant1.D12_PWM, LED3.E
  N9: Composant1.D13_PWM, LED3.D
  N10: Composant1.D3_PWM, LED2.anode
  N11: Composant1.D4_PWM/SS1, LED1.anode
  N12: Composant1.D5_PWM, S1.Pin_3, S1.Pin_4, R3.Pin_0
  N13: Composant1.D6_PWM, LED3.G
  N14: Composant1.D7_PWM, LED3.F
  N15: Composant1.D22, J1.pin2
  N16: Composant1.D30, LED6.anode
  N17: Composant1.D32, LED5.anode
  N18: Composant1.D34, LED4.anode
  N19: Composant1.D36, LED3.DIG4
  N20: Composant1.D38, R10.Pin_1
  N21: Composant1.D40, R8.Pin_0
  N22: Composant1.D42, R9.Pin_0
  N23: Composant1.GND, R1.Pin_0, R2.Pin_1, R3.Pin_1, S2.Pin_1, S2.Pin_2, R11.Pin_0, R13.Pin_0, R15.Pin_0, R16.Pin_0, R17.Pin_0, R18.Pin_0, J1.pin1, R19.Pin_0
  N24: R1.Pin_1, LED1.cathode
  N25: LED2.cathode, R2.Pin_0
  N26: LED3.DIG3, R4.Pin_0, R5.Pin_1
  N27: LED3.COL-C, R10.Pin_0
  N28: LED3.C, R8.Pin_1
  N29: LED3.B, R9.Pin_1
  N30: LED4.cathode, R11.Pin_1
  N31: LED5.cathode, R12.Pin_1
  N32: LED6.cathode, R13.Pin_1
  N33: S3.Pin_1, S3.Pin_2, R16.Pin_1
  N34: S4.Pin_1, S4.Pin_2, R19.Pin_1
  N35: S5.Pin_1, S5.Pin_2, R17.Pin_1
  N36: S6.Pin_1, S6.Pin_2, R18.Pin_1
  N37: S7.Pin_1, S7.Pin_2, R15.Pin_1

notes:
  42 = 2 , 40 = 3, 38 = 4 , 36 = 5
