# Fritzing sketch schema_a_finir (saved by Fritzing 0.9.3b)
breadboards: 3

parts:
  Composant1 = Arduino Due (Rev2b)
  R1 = Resistor [tolerance=±5% resistance=220 package=THT]  # not connected
  LED1 = LED - 5mm [color="Yellow (595nm)" package="5 mm [THT]"]
  LED2 = LED - 5mm [color="Red (633nm)" package="5 mm [THT]"]
  R2 = Resistor [tolerance=±5% resistance=220 package=THT]
  R3 = Resistor [tolerance=±5% resistance=220 package=THT]  # not connected
  LED3 = 7-SEGMENT-4DIGIT-YOUNGSUN [package=7-segment-4digit-youngsun]
  S2 = Pushbutton [package="[THT]"]
  LED4 = LED - 5mm [color="Yellow (595nm)" package="5 mm [THT]"]  # not connected
  LED5 = LED - 5mm [color="Green (570nm)" package="5 mm [THT]"]
  LED6 = LED - 5mm [color="Red (635nm)" package="5 mm [THT]"]
  R11 = Resistor [tolerance=±5% resistance=220 package=THT]
  R12 = Resistor [tolerance=±5% resistance=220 package=THT]
  R13 = Resistor [tolerance=±5% resistance=220 package=THT]
  S3 = Pushbutton [package="[THT]"]
  S4 = Pushbutton [package="[THT]"]
  S5 = Pushbutton [package="[THT]"]
  S6 = Pushbutton [package="[THT]"]
  S7 = Pushbutton [package="[THT]"]
  R14 = Resistor [tolerance=±2% resistance=1k package=THT]
  R16 = Resistor [tolerance=±5% resistance=560 package=THT]
  R17 = Resistor [tolerance=±5% resistance=4.7k package=THT]
  R18 = Resistor [tolerance=±5% resistance=10k package=THT]
  J1 = Piezo Speaker
  R19 = Resistor [tolerance=±5% resistance=1k package=THT]
  R15 = Resistor [tolerance=±5% resistance=220 power=1kW package=THT]
  LED7 = LED - 5mm [color="Red (633nm)" package="5 mm [THT]"]
  LED8 = LED - 5mm [color="Green (570nm)" package="5 mm [THT]"]
  R20 = Resistor [tolerance=±5% resistance=220 package=THT]
  R21 = Resistor [tolerance=±5% resistance=220 package=THT]
  LED9 = LED - 5mm [color="Blue (525nm)" package="5 mm [THT]"]  # not connected
  R22 = Resistor [tolerance=±5% resistance=220 package=THT]
  LED10 = LED - 5mm [color="Yellow (595nm)" package="5 mm [THT]"]
  LED11 = LED - 5mm [color="Yellow (595nm)" package="5 mm [THT]"]
  S8 = Pushbutton [package="[THT]"]
  R23 = Resistor [tolerance=±5% resistance=220 package=THT]
  R24 = Resistor [tolerance=±5% resistance=220 package=THT]
  R25 = Resistor [tolerance=±5% resistance=220 package=THT]
  R26 = Resistor [tolerance=±5% resistance=220 package=THT]
  U1 = LCD-16X2 [package=lcd-16x2_noholes]
  S9 = Pushbutton [package="[THT]"]
  J2 = Piezo Speaker
  R27 = Resistor [tolerance=±5% resistance=220 package=THT]
  R28 = Resistor [tolerance=±5% resistance=220 package=THT]
  R29 = Resistor [tolerance=±5% resistance=220 package=THT]
  R30 = Resistor [tolerance=±5% resistance=220 package=THT]
  R31 = Resistor [tolerance=±5% resistance=220 package=THT]
  R32 = Resistor [tolerance=±5% resistance=220 package=THT]

nets:
  N1: Composant1.A1, S3.Pin_1, S3.Pin_2, S4.Pin_1, S4.Pin_2, S5.Pin_1, S5.Pin_2, S6.Pin_1, S6.Pin_2, S7.Pin_1, S7.Pin_2, R14.Pin_0
  N2: Composant1.D14/TX3, LED5.anode
  N3: Composant1.D17/RX2, LED7.anode
  N4: Composant1.D18/TX1, LED8.anode
  N5: Composant1.D19/RX1, LED6.anode
  N6: Composant1.D20/SDA3, U1.VO
  N7: Composant1.D21/SCL3, U1.RS
  N8: Composant1.IOREF, R14.Pin_1, J1.pin2
  GND: Composant1.GND, R2.Pin_0, R23.Pin_0, R24.Pin_0, R25.Pin_0, R26.Pin_0, U1.VSS, J2.pin1, R32.Pin_0
  N9: Composant1.D8_PWM, LED3.DIG3
  N10: Composant1.D9_PWM, LED3.COL-A, R28.Pin_0
  N11: Composant1.D10_PWM/SS0, LED3.D
  N12: Composant1.D11_PWM, LED3.COL-C
  N13: Composant1.D12_PWM, LED3.DP
  N14: Composant1.D13_PWM, LED3.E
  N15: Composant1.SCL1, R11.Pin_1, R12.Pin_1, R13.Pin_1, R16.Pin_1, R17.Pin_1, R18.Pin_0, J1.pin1, R19.Pin_1, R15.Pin_0, R20.Pin_0, R21.Pin_0, R22.Pin_1
  N16: Composant1.D2_PWM, R31.Pin_0
  N17: Composant1.D3_PWM, R30.Pin_0
  N18: Composant1.D4_PWM/SS1, R29.Pin_1
  N19: Composant1.D5_PWM, R27.Pin_1
  N20: Composant1.D6_PWM, LED3.C
  N21: Composant1.D7_PWM, LED3.APOS-C
  N22: Composant1.D44, LED11.anode
  N23: Composant1.D45, S8.Pin_3, S8.Pin_4, R26.Pin_1
  N24: Composant1.D46, LED10.anode
  N25: Composant1.D47, S2.Pin_3, S2.Pin_4, R25.Pin_1
  N26: Composant1.D48, S9.Pin_1, S9.Pin_2, R32.Pin_1
  N27: Composant1.D49, LED2.anode
  N28: Composant1.D50, J2.pin2
  N29: Composant1.D51, LED1.anode
  N30: LED2.cathode, R2.Pin_1
  N31: LED3.DIG4, R27.Pin_0, R28.Pin_1
  N32: LED3.APOS-A, R29.Pin_0
  N33: LED3.F, R30.Pin_1
  N34: LED3.A, R31.Pin_1
  N35: S2.Pin_1, S2.Pin_2, S8.Pin_1, S8.Pin_2, U1.VDD, S9.Pin_3, S9.Pin_4
  N36: LED5.cathode, R13.Pin_0
  N37: LED6.cathode, R12.Pin_0
  N38: S3.Pin_3, S3.Pin_4, R17.Pin_0
  N39: S4.Pin_3, S4.Pin_4, R19.Pin_0
  N40: S5.Pin_3, S5.Pin_4, R16.Pin_0
  N41: S6.Pin_3, S6.Pin_4
  N42: S7.Pin_3, S7.Pin_4
  N43: LED7.cathode, R20.Pin_1
  N44: LED8.cathode, R21.Pin_1
  N45: LED10.cathode, R23.Pin_1
  N46: LED11.cathode, R24.Pin_1

notes:
  le piezo a 3 pins en vrai
