# Fritzing sketch morse (saved by Fritzing 0.9.3b)
breadboards: 1

parts:
  Composant1 = Arduino Due (Rev2b)
  R1 = Resistor [tolerance=±5% resistance=220 package=THT]
  LED1 = LED - 5mm [color="Red (633nm)" package="5 mm [THT]"]
  LED2 = LED - 5mm [color="Red (633nm)" package="5 mm [THT]"]
  R2 = Resistor [tolerance=±5% resistance=220 package=THT]
  S1 = Pushbutton [package="[THT]"]
  R3 = Resistor [tolerance=±5% resistance=220 package=THT]

nets:
  N1: Composant1.IOREF, S1.Pin_1, S1.Pin_2
  N2: Composant1.D8_PWM, R2.Pin_1
  N3: Composant1.D9_PWM, S1.Pin_3, S1.Pin_4, R3.Pin_0
  N4: Composant1.D7_PWM, LED1.anode
  N5: Composant1.GND, R1.Pin_0, LED2.cathode, R3.Pin_1
  N6: R1.Pin_1, LED1.cathode
  N7: LED2.anode, R2.Pin_0
