# Fritzing sketch timer (saved by Fritzing 0.9.3b)
breadboards: 1

parts:
  R1 = Resistor [tolerance=±5% resistance=220 package=THT]
  R2 = Resistor [tolerance=±5% resistance=220 package=THT]
  LED1 = 7-SEGMENT-4DIGIT-YOUNGSUN [package=7-segment-4digit-youngsun-longpads]
  R3 = Resistor [tolerance=±5% resistance=220 package=THT]
  R4 = Resistor [tolerance=±5% resistance=220 package=THT]
  R5 = Resistor [tolerance=±5% resistance=220 package=THT]
  Composant1 = Arduino Due (Rev2b)
  J1 = Piezo Speaker
  S1 = Pushbutton [package="[THT]"]
  LED2 = LED - 5mm [color="Red (633nm)" package="5 mm [THT]"]
  R6 = Resistor [tolerance=±5% resistance=220 package=THT]
  R7 = Resistor [tolerance=±5% resistance=220 package=THT]

nets:
  N1: R1.Pin_0, Composant1.D5_PWM
  N2: R1.Pin_1, R2.Pin_0, LED1.B
  N3: R2.Pin_1, LED1.COL-C, Composant1.D9_PWM
  N4: LED1.DIG1, Composant1.D7_PWM
  N5: LED1.DIG2, R5.Pin_1
  N6: LED1.D, R4.Pin_0
  N7: LED1.COL-A, Composant1.D11_PWM
  N8: LED1.E, Composant1.D6_PWM
  N9: LED1.DIG3, R3.Pin_0
  N10: LED1.F, Composant1.D10_PWM/SS0
  N11: LED1.C, Composant1.D13_PWM
  N12: LED1.A, Composant1.D8_PWM
  N13: LED1.G, Composant1.D12_PWM
  N14: R3.Pin_1, Composant1.D2_PWM
  N15: R4.Pin_1, Composant1.D3_PWM
  N16: R5.Pin_0, Composant1.D4_PWM/SS1
  N17: Composant1.D21/SCL3, S1.Pin_3, S1.Pin_4, R7.Pin_0
  N18: Composant1.5V, J1.pin2, LED2.anode, R7.Pin_1
  N19: Composant1.GND, J1.pin1, S1.Pin_1, S1.Pin_2
  N20: Composant1.D47, R6.Pin_0
  N21: LED2.cathode, R6.Pin_1

notes:
  Piezo = signal en jaune
